// Logisim project 16bitprocessor.circ as structural Verilog: 7 circuits, main circuit main
module main (
  input  PC_R,
  input  PC_LDE,
  input  [7:0] PC_LD,
  input  PC_OE,
  input  IR_WE,
  input  IR_R,
  input  IR_OE,
  input  GPR_WE,
  input  [3:0] GPR_SEL,
  input  GPR_OE,
  input  RA_WE,
  input  RA_R,
  input  RA_OE,
  input  ALU_CIN,
  input  [2:0] ALU_SEL,
  input  ALU_WE,
  input  RB_WE,
  input  RB_R,
  input  RB_OE,
  input  MBR_WE,
  input  MBR_R,
  input  MBR_OE,
  input  MAR_WE,
  input  MAR_R,
  input  MAR_OE,
  input  [15:0] IDB,
  input  [7:0] IAB,
  output [7:0] out_28,
  output [7:0] PC_S,
  output [15:0] out_30,
  output [15:0] out_31,
  output [15:0] REGA_S,
  output [15:0] MD,
  output [15:0] ALU_S,
  output [15:0] REGB_S
);

  wire Arithmetic_Logic_Unit_c, Arithmetic_Logic_Unit_z, clock_1_out;
  wire [15:0] Instruction_Register_o, Register_A_o, Register_B_o;

  Clock clock_1 (.out(clock_1_out));
  Program_Counter program_counter_1 (
    .R(PC_R), .LDE(PC_LDE), .CLK(clock_1_out), .OE(PC_OE), .LD(PC_LD), .O(IAB), .S(PC_S));
  Register_16bit Instruction_Register (
    .D(IDB), .WE(IR_WE), .CLK(clock_1_out), .R(IR_R), .OE(IR_OE), .O(Instruction_Register_o), .S(out_30));
  General_Purpose_Registers GPR (.CLK(clock_1_out), .WE(GPR_WE), .INP(IDB), .SEL(GPR_SEL), .OE(GPR_OE), .O(IDB));
  Register_16bit Register_A (
    .D(IDB), .WE(RA_WE), .CLK(clock_1_out), .R(RA_R), .OE(RA_OE), .O(Register_A_o), .S(REGA_S));
  ALU Arithmetic_Logic_Unit (
    .c_in(ALU_CIN), .SEL(ALU_SEL), .A(Register_A_o), .B(Register_B_o), .OE(ALU_WE), .O(IDB), .S(ALU_S),
    .Z(Arithmetic_Logic_Unit_z), .C(Arithmetic_Logic_Unit_c), .MD(MD));
  Register_16bit Register_B (
    .D(IDB), .WE(RB_WE), .CLK(clock_1_out), .R(RB_R), .OE(RB_OE), .O(Register_B_o), .S(REGB_S));
  BitSelector #(.group(8), .width(16)) bitselector_1 (.in(Instruction_Register_o), .out(IAB), .sel(1'b0));
  LED Z (.in(Arithmetic_Logic_Unit_z));
  LED C (.in(Arithmetic_Logic_Unit_c));
  Register_8bit Memory_Address_Register (
    .D(IAB), .WE(MAR_WE), .CLK(clock_1_out), .R(MAR_R), .OE(MAR_OE), .O(IAB), .S(out_28));
  Register_16bit Memory_Buffer_Register (
    .D(IDB), .WE(MBR_WE), .CLK(clock_1_out), .R(MBR_R), .OE(MBR_OE), .O(IDB), .S(out_31));
  RAM #(.dataWidth(16), .enables("line")) INS_RAM (.clk(clock_1_out));  // open: addr, we, din, dout
  RAM #(.dataWidth(16), .enables("line")) DAT_RAM (.clk(clock_1_out));  // open: addr, we, din, dout
endmodule

module Register_16bit (
  input  [15:0] D,
  input  WE,
  input  CLK,
  input  R,
  input  OE,
  output [15:0] O,
  output [15:0] S
);

  Register #(.width(16)) register_1 (.D(D), .en(WE), .clk(CLK), .Q(S), .clr(R));
  assign O = OE ? S : 16'bz;  // Controlled_Buffer controlled_buffer_1
endmodule

module Register_8bit (
  input  [7:0] D,
  input  WE,
  input  CLK,
  input  R,
  input  OE,
  output [7:0] O,
  output [7:0] S
);

  Register register_1 (.D(D), .en(WE), .clk(CLK), .Q(S), .clr(R));
  assign O = OE ? S : 8'bz;  // Controlled_Buffer controlled_buffer_1
endmodule

module ALU (
  input  c_in,
  input  [2:0] SEL,
  input  [15:0] A,
  input  [15:0] B,
  input  OE,
  output [15:0] O,
  output [15:0] S,
  output Z,
  output C,
  output [15:0] MD
);

  wire adder_1_cout, subtractor_1_bout;
  wire [3:0] bitselector_1_out, bitselector_2_out;
  wire [15:0] adder_1_out, and_1_out, divider_1_out, divider_1_rem, multiplier_1_cout, multiplier_1_out,
       or_1_out, shifter_1_out, shifter_2_out, subtractor_1_out;

  BitSelector #(.group(4), .width(16)) bitselector_1 (.in(B), .out(bitselector_1_out), .sel(2'b00));
  BitSelector #(.group(4), .width(16)) bitselector_2 (.in(B), .out(bitselector_2_out), .sel(2'b00));
  Adder #(.width(16)) adder_1 (.a(A), .b(B), .out(adder_1_out), .cin(c_in), .cout(adder_1_cout));
  Subtractor #(.width(16)) subtractor_1 (.a(A), .b(B), .out(subtractor_1_out), .bin(c_in), .bout(subtractor_1_bout));
  Multiplier #(.width(16)) multiplier_1 (.a(A), .b(B), .out(multiplier_1_out), .cout(multiplier_1_cout));  // open: cin
  Divider #(.width(16)) divider_1 (.a(A), .b(B), .out(divider_1_out), .rem(divider_1_rem));  // open: upper
  Shifter #(.width(16)) shifter_1 (.in(A), .\dist (bitselector_1_out), .out(shifter_1_out));
  Shifter #(.shift("lr"), .width(16)) shifter_2 (.in(A), .\dist (bitselector_2_out), .out(shifter_2_out));
  assign and_1_out = A & B;  // AND_Gate and_1, 16 bits wide
  assign or_1_out = A | B;  // OR_Gate or_1, 16 bits wide
  Multiplexer #(.select(3), .width(16)) multiplexer_1 (
    .in0(adder_1_out), .in1(subtractor_1_out), .in2(multiplier_1_out), .in3(divider_1_out),
    .in4(shifter_1_out), .in5(shifter_2_out), .in6(and_1_out), .in7(or_1_out), .out(S), .sel(SEL));
  Multiplexer #(.select(3)) multiplexer_2 (
    .in0(adder_1_cout), .in1(subtractor_1_bout), .in2(1'b0), .in3(1'b0), .in4(1'b0), .in5(1'b0), .in6(1'b0),
    .in7(1'b0), .out(C), .sel(SEL));
  Multiplexer #(.select(3), .width(16)) multiplexer_3 (
    .in0({16{1'b0}}), .in1({16{1'b0}}), .in2(multiplier_1_cout), .in3(divider_1_rem), .in4({16{1'b0}}),
    .in5({16{1'b0}}), .in6({16{1'b0}}), .in7({16{1'b0}}), .out(MD), .sel(SEL));
  assign O = OE ? S : 16'bz;  // Controlled_Buffer controlled_buffer_1
  zero_checker zero_checker_1 (.I(S), .Z(Z));
endmodule

module zero_checker (
  input  [15:0] I,
  output Z
);

  nor nor_1 (Z, I[0], I[1], I[2], I[3], I[4], I[5], I[6], I[7], I[8], I[9], I[10], I[11], I[12], I[13], I[14], I[15]);
endmodule

module Program_Counter (
  input  R,
  input  LDE,
  input  CLK,
  input  [7:0] LD,
  input  OE,
  output [7:0] O,
  output [7:0] S
);

  Counter counter_1 (.clr(R), .load(LDE), .clk(CLK), .D(LD), .Q(S));  // open: up, count, carry
  assign O = OE ? S : 8'bz;  // Controlled_Buffer controlled_buffer_1
endmodule

module General_Purpose_Registers (
  input  WE,
  input  [3:0] SEL,
  input  CLK,
  input  [15:0] INP,
  input  OE,
  output [15:0] O
);

  wire demultiplexer_1_out0, demultiplexer_1_out1, demultiplexer_1_out2, demultiplexer_1_out3,
       demultiplexer_1_out4, demultiplexer_1_out5, demultiplexer_1_out6, demultiplexer_1_out7,
       demultiplexer_1_out8, demultiplexer_1_out9, demultiplexer_1_out10, demultiplexer_1_out11,
       demultiplexer_1_out12, demultiplexer_1_out13, demultiplexer_1_out14, demultiplexer_1_out15;
  wire [15:0] multiplexer_1_out, R0_o, R1_o, R2_o, R3_o, R4_o, R5_o, R6_o, R7_o, R8_o, R9_o, R10_o, R11_o,
       R12_o, R13_o, R14_o, R15_o;

  Register_16bit R0 (.D(INP), .WE(demultiplexer_1_out0), .CLK(CLK), .O(R0_o));  // open: R, OE, S
  Register_16bit R1 (.D(INP), .WE(demultiplexer_1_out1), .CLK(CLK), .O(R1_o));  // open: R, OE, S
  Register_16bit R2 (.D(INP), .WE(demultiplexer_1_out2), .CLK(CLK), .O(R2_o));  // open: R, OE, S
  Register_16bit R3 (.D(INP), .WE(demultiplexer_1_out3), .CLK(CLK), .O(R3_o));  // open: R, OE, S
  Register_16bit R4 (.D(INP), .WE(demultiplexer_1_out4), .CLK(CLK), .O(R4_o));  // open: R, OE, S
  Register_16bit R5 (.D(INP), .WE(demultiplexer_1_out5), .CLK(CLK), .O(R5_o));  // open: R, OE, S
  Register_16bit R6 (.D(INP), .WE(demultiplexer_1_out6), .CLK(CLK), .O(R6_o));  // open: R, OE, S
  Register_16bit R7 (.D(INP), .WE(demultiplexer_1_out7), .CLK(CLK), .O(R7_o));  // open: R, OE, S
  Demultiplexer #(.select(4)) demultiplexer_1 (
    .out0(demultiplexer_1_out0), .out1(demultiplexer_1_out1), .out2(demultiplexer_1_out2),
    .out3(demultiplexer_1_out3), .out4(demultiplexer_1_out4), .out5(demultiplexer_1_out5),
    .out6(demultiplexer_1_out6), .out7(demultiplexer_1_out7), .out8(demultiplexer_1_out8),
    .out9(demultiplexer_1_out9), .out10(demultiplexer_1_out10), .out11(demultiplexer_1_out11),
    .out12(demultiplexer_1_out12), .out13(demultiplexer_1_out13), .out14(demultiplexer_1_out14),
    .out15(demultiplexer_1_out15), .in(WE), .sel(SEL));
  Register_16bit R8 (.D(INP), .WE(demultiplexer_1_out8), .CLK(CLK), .O(R8_o));  // open: R, OE, S
  Register_16bit R9 (.D(INP), .WE(demultiplexer_1_out9), .CLK(CLK), .O(R9_o));  // open: R, OE, S
  Register_16bit R10 (.D(INP), .WE(demultiplexer_1_out10), .CLK(CLK), .O(R10_o));  // open: R, OE, S
  Register_16bit R11 (.D(INP), .WE(demultiplexer_1_out11), .CLK(CLK), .O(R11_o));  // open: R, OE, S
  Register_16bit R12 (.D(INP), .WE(demultiplexer_1_out12), .CLK(CLK), .O(R12_o));  // open: R, OE, S
  Register_16bit R13 (.D(INP), .WE(demultiplexer_1_out13), .CLK(CLK), .O(R13_o));  // open: R, OE, S
  Register_16bit R14 (.D(INP), .WE(demultiplexer_1_out14), .CLK(CLK), .O(R14_o));  // open: R, OE, S
  Register_16bit R15 (.D(INP), .WE(demultiplexer_1_out15), .CLK(CLK), .O(R15_o));  // open: R, OE, S
  Multiplexer #(.select(4), .width(16)) multiplexer_1 (
    .in0(R0_o), .in1(R1_o), .in2(R2_o), .in3(R3_o), .in4(R4_o), .in5(R5_o), .in6(R6_o), .in7(R7_o),
    .in8(R8_o), .in9(R9_o), .in10(R10_o), .in11(R11_o), .in12(R12_o), .in13(R13_o), .in14(R14_o),
    .in15(R15_o), .out(multiplexer_1_out), .sel(SEL));
  assign O = OE ? multiplexer_1_out : 16'bz;  // Controlled_Buffer controlled_buffer_1
endmodule
